# Fritzing sketch CorsairController (saved by Fritzing 0.9.3b)
stripboards: 2

parts:
  Pro_Micro = Pro Micro
  Power-In-Micro = female pin header, 3 pins [form="♀ (female)"]
  ARGB-Out = female pin header, 2 pins [form="♀ (female)"]
  Fans-Out = female pin header, 4 pins [form="♀ (female)"]
  RGB-Out = female pin header, 3 pins [form="♀ (female)"]
  UART-Out = female pin header, 2 pins [form="♀ (female)"]
  Power-In = female pin header, 3 pins [form="♀ (female)"]
  R = Basic FET N-Channel [package="TO220 [THT]"]
  G = Basic FET N-Channel [package="TO220 [THT]"]
  B = Basic FET N-Channel [package="TO220 [THT]"]
  UART-Out_2 = female pin header, 5 pins [form="♀ (female)"]
  RGB-Out_2 = female pin header, 4 pins [form="♀ (female)"]
  Power-Out-Fans = female pin header, 2 pins [form="♀ (female)"]
  ARGB1-Out = female pin header, 3 pins [form="♀ (female)"]
  ARGB2-Out = female pin header, 3 pins [form="♀ (female)"]
  RGB-In = male pin header, 3 pins [form="♂ (male)"]
  ARGB-In = male pin header, 2 pins [form="♂ (male)"]
  UART-In = male pin header, 2 pins [form="♂ (male)"]
  Power-Out-Micro = male pin header, 1 pin [form="♂ (male)"]
  Power-In-Fans = male pin header, 2 pins [form="♂ (male)"]
  Fans-In = male pin header, 4 pins [form="♂ (male)"]
  S1 = Toggle Switch [package=THT]
  F1 = Basic FET N-Channel [package="TO220 [THT]"]
  F1_2 = female pin header, 4 pins [form="♀ (female)"]
  F2 = female pin header, 4 pins [form="♀ (female)"]
  S2 = Toggle Switch [package=THT]
  F2_2 = Basic FET N-Channel [package="TO220 [THT]"]

nets:
  N1: Pro_Micro.TX1, UART-Out.pin2
  N2: Pro_Micro.RX0, UART-Out.pin1
  N3: Pro_Micro.D2, Fans-Out.pin4
  N4: Pro_Micro.D3, Fans-Out.pin1
  N5: Pro_Micro.D4, ARGB-Out.pin1
  N6: Pro_Micro.D5, Fans-Out.pin3
  N7: Pro_Micro.D6, RGB-Out.pin1
  N8: Pro_Micro.D7, Fans-Out.pin2
  N9: Pro_Micro.D8, ARGB-Out.pin2
  N10: Pro_Micro.D9, RGB-Out.pin2
  N11: Pro_Micro.D10, RGB-Out.pin3
  N12: Pro_Micro.VCC, Power-In-Micro.pin2
  N13: Pro_Micro.GND, Power-In-Micro.pin3
  N14: Pro_Micro.RAW, Power-In-Micro.pin1
  N15: Power-In.pin1, UART-Out_2.pin1, RGB-Out_2.pin1, Power-Out-Fans.pin1, ARGB1-Out.pin1, ARGB2-Out.pin1
  N16: Power-In.pin2, UART-Out_2.pin2
  N17: Power-In.pin3, R.source, G.source, B.source, UART-Out_2.pin5, Power-Out-Fans.pin2, ARGB1-Out.pin3, ARGB2-Out.pin3, Power-Out-Micro.pin1
  N18: R.gate, RGB-In.pin1
  N19: R.drain, RGB-Out_2.pin2
  N20: G.gate, RGB-In.pin2
  N21: G.drain, RGB-Out_2.pin3
  N22: B.gate, RGB-In.pin3
  N23: B.drain, RGB-Out_2.pin4
  N24: UART-Out_2.pin3, UART-In.pin1
  N25: UART-Out_2.pin4, UART-In.pin2
  N26: ARGB1-Out.pin2, ARGB-In.pin1
  N27: ARGB2-Out.pin2, ARGB-In.pin2
  N28: Power-In-Fans.pin1, F1_2.pin3, F2.pin3
  N29: Power-In-Fans.pin2, S1.L1, F1.source, S2.L1, F2_2.source
  N30: Fans-In.pin1, F1.gate, F1_2.pin1
  N31: Fans-In.pin2, F1_2.pin2
  N32: Fans-In.pin3, F2.pin1, F2_2.gate
  N33: Fans-In.pin4, F2.pin2
  N34: S1.COM, F1_2.pin4
  N35: S1.L2, F1.drain
  N36: F2.pin4, S2.COM
  N37: S2.L2, F2_2.drain

notes:
  RGB Board, Protoboard for controlling RGB strips and power distribution, 0.2
  Controller Board, Wiring for Arduino Pro Micro, 0.2
  Fan Board, Protoboard for controlling 3-pin and 4-pin fans, 0.2

custom parts:
  Pro Micro: The SparkFun Pro Micro is a complete USB-based microcontoller development system, in a very small footprint, capable of implementing many types of projects. All programming can be done via the USB port.
