# Fritzing sketch LightingController (saved by Fritzing 0.9.3b)
stripboards: 1

parts:
  Pro_Micro = Pro Micro
  Power_Input = screw terminal, 3 pins
  ARGB1 = female pin header, 3 pins [form="♀ (female)"]
  ARGB2 = female pin header, 3 pins [form="♀ (female)"]
  RGB = female pin header, 4 pins [form="♀ (female)"]
  R = Basic FET N-Channel [package="TO220 [THT]"]
  G = Basic FET N-Channel [package="TO220 [THT]"]
  B = Basic FET N-Channel [package="TO220 [THT]"]

nets:
  N1: Pro_Micro.D2, ARGB1.pin2
  N2: Pro_Micro.D4, ARGB2.pin2
  N3: Pro_Micro.D6, R.gate
  N4: Pro_Micro.D9, G.gate
  N5: Pro_Micro.D10, B.gate
  N6: Pro_Micro.GND, Power_Input.pin3, ARGB1.pin1, ARGB2.pin1, R.source, G.source, B.source
  N7: Pro_Micro.RAW, Power_Input.pin1, ARGB1.pin3, ARGB2.pin3, RGB.pin1
  N8: RGB.pin2, R.drain
  N9: RGB.pin3, G.drain
  N10: RGB.pin4, B.drain

custom parts:
  Pro Micro: The SparkFun Pro Micro is a complete USB-based microcontoller development system, in a very small footprint, capable of implementing many types of projects. All programming can be done via the USB port.
